# Fritzing sketch Temp Sensor Boot aussen (saved by Fritzing 0.9.4)

parts:
  Bauteil1 = Arduino Pro Mini v13
  DS2 = DS18B20 1-Wire Temperature Sensor [part_number=DS18B20]
  LCD1 = LCD screen
  LCM1602_IIC1 = LCM1602 IIC [part_number="LCM1602 IIC" chip_label="LCM1602 IIC" package="DIP (Dual Inline) [THT]"]
  R3 = Resistor [tolerance=±5% resistance=4.7k package="0402 [SMD]"]
  DHT1 = DHT22 Humidity and Temperature Sensor
  R8 = Resistor [tolerance=±5% resistance=4.7k package="0402 [SMD]"]
  U1 = Voltage Regulator - 5V [package="TO220 [THT]"]
  C1 = Ceramic Capacitor [capacitance=100nF package="100 mil [THT, multilayer]"]
  C2 = Ceramic Capacitor [capacitance=100nF package="100 mil [THT, multilayer]"]
  C3 = Electrolytic Capacitor [capacitance=10µF package="100 mil [THT, electrolytic]"]
  J1 = Screw terminal - 2 pins [package=THT]
  R9 = Photocell (LDR) [package=THT]
  R10 = Resistor [tolerance=±5% resistance=1k package="0402 [SMD]"]
  R11 = Resistor [tolerance=±5% resistance=220 package="0402 [SMD]"]
  R12 = Resistor [tolerance=±5% resistance=4.7k package="0402 [SMD]"]
  R13 = Resistor [tolerance=±5% resistance=4.7k package="0402 [SMD]"]
  R14 = Resistor [tolerance=±5% resistance=10k package="0402 [SMD]"]
  R15 = Resistor [tolerance=±5% resistance=10k package="0402 [SMD]"]

nets:
  N1: Bauteil1.A4, R13.Pin_0, R14.Pin_0
  N2: Bauteil1.A5, R12.Pin_0, R15.Pin_0
  N3: Bauteil1.RAW, LCM1602_IIC1.VCC, U1.output_voltage, C1.1, C3.+, R9.pin_1
  GND: Bauteil1.GND, DS2.GND, LCM1602_IIC1.GND, DHT1.GND, U1.GND, C1.0, C2.0, C3.-, J1.pin1, R10.Pin_0, R14.Pin_1, R15.Pin_1
  VDD: Bauteil1.VCC, DS2.VDD, R3.Pin_1, DHT1.VDD, R8.Pin_1
  N4: Bauteil1.A3, R9.pin_0, R10.Pin_1
  N5: Bauteil1.D9_PWM, R11.Pin_0
  N6: Bauteil1.D8, DHT1.DATA, R8.Pin_0
  N7: Bauteil1.D3_PWM, DS2.DQ, R3.Pin_0
  VSS: LCD1.VSS, LCM1602_IIC1.VSS
  VDD_2: LCD1.VDD, LCM1602_IIC1.VDD
  N8: LCD1.V0, LCM1602_IIC1.V0
  N9: LCD1.RS, LCM1602_IIC1.RS
  N10: LCD1.R/W, LCM1602_IIC1.RW
  N11: LCD1.E, LCM1602_IIC1.E
  N12: LCD1.DB0, LCM1602_IIC1.D0
  N13: LCD1.DB1, LCM1602_IIC1.D1
  N14: LCD1.DB2, LCM1602_IIC1.D2
  N15: LCD1.DB3, LCM1602_IIC1.D3
  N16: LCD1.DB4, LCM1602_IIC1.D4
  N17: LCD1.DB5, LCM1602_IIC1.D5
  N18: LCD1.DB6, LCM1602_IIC1.D6
  N19: LCD1.DB7, LCM1602_IIC1.D7
  N20: LCD1.LED-, LCM1602_IIC1.A
  N21: LCD1.LED+, LCM1602_IIC1.K
  N22: LCM1602_IIC1.SDA, R13.Pin_1
  N23: LCM1602_IIC1.SCL, R12.Pin_1
  N24: U1.input_voltage, C2.1, J1.pin2

notes:
  Temp innen
  5,0V
  4,7k
  Arduino mini pro (3,3V)
  3-fach Temp Anzeige für Boot aussen
  Temp. aussen
  LCD 4x20
  12V in
  DS1820B
  --------
  Temp. innen
  Feuchte innen
  LM 7805
  DHT22
  100 nF
  10 uF
  LDR
  1k
  220
  Pin 7 vom U1 entlöten.
  Diese Leitung an die Basis von Q1 anlöten
  Damit wird das Display gedimmt
  2 x 4,7k
  2 x 10k

custom parts:
  LCD screen: A standard character display, usually with 2x16 characters. Comes in many colors.
  LCM1602 IIC: I2C-Module to use a 1602 or 2004 LCD on with the wire.h libory Serial LCD Modul
